// Logisim project control-logic.circ as structural Verilog: 1 circuit, main circuit control_logic
module control_logic (
  input  [31:0] Instruction,
  input  BrEq,
  input  BrLt,
  output PCSel,
  output RegWEn,
  output [2:0] ImmSel,
  output BrUn,
  output ASel,
  output BSel,
  output [3:0] ALUSel,
  output MemWEn,
  output [1:0] WBSel
);

  wire comparator_1_eq, comparator_2_eq, comparator_3_eq, is_sra;

  Multiplexer #(.select(3), .width(4)) multiplexer_1 (
    .in0(4'b0000), .in1(4'b0001), .in2(4'b0010), .in4(4'b0100), .in5(4'b0101), .in6(4'b0110), .in7(4'b0111),
    .out(ALUSel), .sel(Instruction[14:12]));  // open: in3
  Comparator #(.width(3)) comparator_1 (.a(Instruction[14:12]), .b(3'b101), .eq(comparator_1_eq));  // open: gt, lt
  Comparator #(.width(7)) comparator_2 (.a(Instruction[31:25]), .b(7'b0100000), .eq(comparator_2_eq));  // open: gt, lt
  and and_1 (is_sra, comparator_1_eq, comparator_2_eq);
  Comparator #(.width(7)) comparator_3 (.a(Instruction[6:0]), .b(7'b0010011), .eq(comparator_3_eq));  // open: gt, lt
  Multiplexer #(.width(2)) multiplexer_2 (.in0(2'b00), .in1(2'b01));  // open: out, sel
  Comparator #(.width(7)) comparator_4 (.a(Instruction[6:0]), .b(7'b0010011), .eq(BSel));  // open: gt, lt

  assign ImmSel = 3'b000;
  assign PCSel = 1'b0;
  assign RegWEn = 1'b1;
  assign WBSel = 2'b01;

  // Other names for the same wires on the sheet: opcode[6:0] = Instruction[6:0]; rd[4:0] = Instruction[11:7];
  //   funct3[2:0] = Instruction[14:12]; rs1[4:0] = Instruction[19:15]; rs2[4:0] = Instruction[24:20];
  //   funct7[6:0] = Instruction[31:25]

  // Notes on the sheet:
  //   Decode
  //   add
  //   sll
  //   slt
  //   xor
  //   srl
  //   or
  //   and
  //   INPUTS to your circuit
  //   DON'T CHANGE THE LOCATIONS OF THE INPUTS AND OUTPUTS!
  //   I-Type
  //   OUTPUT from your circuit
endmodule
